// Logisim project D_FlipFlop_EN.circ as structural Verilog: 3 circuits, main circuit main
module main (
  input  D,
  input  EN,
  input  clk,
  output Q
);

  wire and_1_out, and_2_out;

  and and_1 (and_1_out, D, EN);
  and and_2 (and_2_out, EN, clk);
  D_FlipFlop d_flipflop_1 (.D(and_1_out), .clk(and_2_out), .Q(Q));
endmodule

module D_latch (
  input  WE,
  input  D,
  output Q,
  output Q_bar
);

  wire not_1_out, R_out, S_out;

  not not_1 (not_1_out, D);
  and S (S_out, not_1_out, WE);
  and R (R_out, WE, D);
  nor nor_1 (Q, S_out, Q_bar);
  nor nor_2 (Q_bar, R_out, Q);
endmodule

module D_FlipFlop (
  input  D,
  input  clk,
  output Q
);

  wire d_latch_1_q, not_1_out;

  not not_1 (not_1_out, clk);
  D_latch d_latch_1 (.WE(D), .D(not_1_out), .Q(d_latch_1_q));  // open: Q_bar
  D_latch d_latch_2 (.WE(d_latch_1_q), .D(clk), .Q(Q));  // open: Q_bar
endmodule
