// Logisim project D_FlipFlop_aBitFlip.circ as structural Verilog: 4 circuits, main circuit main
module main (
  input  R,
  input  clk
);

  wire dff_1_q, dff_2_q, not_1_out;

  DFF dff_1 (.R(R), .D(dff_2_q), .clk(clk), .Q(dff_1_q));  // open: Q_bar
  not not_1 (not_1_out, dff_1_q);
  DFF dff_2 (.R(R), .D(not_1_out), .clk(clk), .Q(dff_2_q));  // open: Q_bar
endmodule

module SR_latch_NOR (
  input  R,
  input  S,
  output Q,
  output Q_bar
);

  nor nor_1 (Q, R, Q_bar);
  nor nor_2 (Q_bar, S, Q);
endmodule

module D_latch (
  input  R,
  input  WE,
  input  D,
  output Q,
  output Q_bar
);

  wire and_1_out, and_2_out, not_1_out, not_2_out, or_1_out;

  not not_1 (not_1_out, R);
  not not_2 (not_2_out, D);
  and and_1 (and_1_out, not_1_out, D, WE);
  and and_2 (and_2_out, WE, not_2_out);
  or or_1 (or_1_out, R, and_2_out);
  SR_latch_NOR sr_latch_nor_1 (.R(or_1_out), .S(and_1_out), .Q(Q), .Q_bar(Q_bar));
endmodule

module DFF (
  input  R,
  input  D,
  input  clk,
  output Q,
  output Q_bar
);

  wire d_latch_1_q, not_1_out;

  not not_1 (not_1_out, clk);
  D_latch d_latch_1 (.R(R), .WE(not_1_out), .D(D), .Q(d_latch_1_q));  // open: Q_bar
  D_latch d_latch_2 (.R(R), .WE(clk), .D(d_latch_1_q), .Q(Q), .Q_bar(Q_bar));
endmodule
