// Logisim project D_latch_1.circ as structural Verilog: 1 circuit, main circuit main
module main (
  input  WE,
  input  D,
  output Q,
  output Q_bar
);

  wire not_1_out, R_out, S_out;

  not not_1 (not_1_out, D);
  and S (S_out, not_1_out, WE);
  and R (R_out, WE, D);
  nor nor_1 (Q, S_out, Q_bar);
  nor nor_2 (Q_bar, R_out, Q);
endmodule
