// Logisim project D_latch_2.circ as structural Verilog: 1 circuit, main circuit main
module main (
  input  D,
  input  WE,
  output Q,
  output Q_bar
);

  wire R_bar_out, S_bar_out;

  nand S_bar (S_bar_out, D, WE);
  nand R_bar (R_bar_out, S_bar_out, WE);
  nand nand_1 (Q, S_bar_out, Q_bar);
  nand nand_2 (Q_bar, R_bar_out, Q);
endmodule
