// Logisim project D_latch_Reset.circ as structural Verilog: 1 circuit, main circuit main
module main (
  input  WE,
  input  D,
  input  Reset,
  output Q,
  output Q_bar
);

  wire not_1_out, not_2_out, R_out, S_out;

  not not_1 (not_1_out, D);
  not not_2 (not_2_out, Reset);
  and S (S_out, not_1_out, WE);
  and R (R_out, WE, not_2_out, D);
  nor nor_1 (Q, S_out, Reset, Q_bar);
  nor nor_2 (Q_bar, R_out, Q);
endmodule
