// Logisim project Enhanced_version_of_sCPU.circ as structural Verilog
module Finger_Pricking (
  input  [3:0] in_1,
  output [7:0] out_2
);

  wire clock_1_out;
  wire [3:0] PC_q;

  Clock clock_1 (.out(clock_1_out));
  Register #(.width(4)) PC (.D(in_1), .en(1'b1), .clk(clock_1_out), .Q(PC_q));  // open: clr
  Multiplexer #(.select(4), .width(8)) multiplexer_1 (
    .in0(8'h86), .in1(8'h92), .in2(8'h1), .in3(8'h90), .in4(8'ha0), .in5(8'hb1), .in6(8'h17), .in7(8'h29),
    .in8(8'hf9), .in9(8'hc3), .out(out_2), .sel(PC_q));  // open: in10, in11, in12, in13, in14, in15
endmodule

module execute (
  input  [7:0] D,
  input  EN,
  input  [1:0] addr,
  output [7:0] out_4
);

  wire and_1_out, and_2_out, and_3_out, and_4_out, clk_out, decoder_1_out0, decoder_1_out1, decoder_1_out2,
       decoder_1_out3;
  wire [7:0] r0_q, r1_q, r2_q, r3_q;

  Clock clk (.out(clk_out));
  Decoder #(.select(2)) decoder_1 (
    .out0(decoder_1_out0), .out1(decoder_1_out1), .out2(decoder_1_out2), .out3(decoder_1_out3), .sel(addr));  // open: en
  Register r0 (.D(D), .en(and_1_out), .clk(clk_out), .Q(r0_q));  // open: clr
  and and_1 (and_1_out, EN, decoder_1_out0);
  and and_2 (and_2_out, EN, decoder_1_out1);
  Register r1 (.D(D), .en(and_2_out), .clk(clk_out), .Q(r1_q));  // open: clr
  Multiplexer #(.select(2), .width(8)) multiplexer_1 (
    .in0(r0_q), .in1(r1_q), .in2(r2_q), .in3(r3_q), .out(out_4), .sel(addr));
  and and_3 (and_3_out, EN, decoder_1_out2);
  Register r2 (.D(D), .en(and_3_out), .clk(clk_out), .Q(r2_q));  // open: clr
  and and_4 (and_4_out, EN, decoder_1_out3);
  Register r3 (.D(D), .en(and_4_out), .clk(clk_out), .Q(r3_q));  // open: clr
endmodule

module li_sCPU (
  input  Reset,
  output [7:0] out_2
);

  wire and_1_out, and_2_out, and_3_out, and_4_out, clk_out, decoder_1_out0, decoder_1_out1, decoder_1_out2,
       decoder_1_out3, xor_1_out;
  wire [3:0] adder_1_out, PC_q;
  wire [7:0] multiplexer_1_out, r0_q, r1_q, r2_q, r3_q, shifter_1_out;

  Adder #(.width(4)) adder_1 (.a(PC_q), .b(4'b0001), .out(adder_1_out));  // open: cin, cout
  Clock clk (.out(clk_out));
  Register #(.width(4)) PC (.D(adder_1_out), .en(1'b1), .clk(clk_out), .Q(PC_q), .clr(Reset));
  Multiplexer #(.select(4), .width(8)) multiplexer_1 (
    .in0(8'h86), .in1(8'h92), .in2(8'h1), .in3(8'h90), .in4(8'ha0), .in5(8'hb1), .in6(8'h17), .in7(8'h29),
    .in8(8'hf9), .in9(8'hc3), .out(multiplexer_1_out), .sel(PC_q));  // open: in10, in11, in12, in13, in14, in15
  xor xor_1 (xor_1_out, multiplexer_1_out[6], multiplexer_1_out[7]);
  Decoder #(.select(2)) decoder_1 (
    .out0(decoder_1_out0), .out1(decoder_1_out1), .out2(decoder_1_out2), .out3(decoder_1_out3),
    .sel(multiplexer_1_out[5:4]));  // open: en
  Shifter shifter_1 (
    .in({{6{1'b0}}, multiplexer_1_out[1:0]}), .\dist ({multiplexer_1_out[3:2], 1'b0}), .out(shifter_1_out));
  and and_1 (and_1_out, xor_1_out, decoder_1_out0);
  Register r0 (.D(shifter_1_out), .en(and_1_out), .clk(clk_out), .Q(r0_q));  // open: clr
  and and_2 (and_2_out, xor_1_out, decoder_1_out1);
  Register r1 (.D(shifter_1_out), .en(and_2_out), .clk(clk_out), .Q(r1_q));  // open: clr
  Multiplexer #(.select(2), .width(8)) multiplexer_2 (
    .in0(r0_q), .in1(r1_q), .in2(r2_q), .in3(r3_q), .out(out_2), .sel(multiplexer_1_out[5:4]));
  Register r2 (.D(shifter_1_out), .en(and_3_out), .clk(clk_out), .Q(r2_q));  // open: clr
  and and_3 (and_3_out, xor_1_out, decoder_1_out2);
  Register r3 (.D(shifter_1_out), .en(and_4_out), .clk(clk_out), .Q(r3_q));  // open: clr
  and and_4 (and_4_out, xor_1_out, decoder_1_out3);
endmodule

module add_sCPU (
  input  Reset
);

  wire and_1_out, and_2_out, and_3_out, and_4_out, clk_out, decoder_1_out0, decoder_1_out2, decoder_2_out0,
       decoder_2_out1, decoder_2_out2, decoder_2_out3, or_1_out, or_2_out;
  wire [3:0] adder_1_out, PC_q;
  wire [7:0] adder_2_out, multiplexer_1_out, multiplexer_2_out, multiplexer_3_out, multiplexer_4_out, r0_q,
       r1_q, r2_q, r3_q, shifter_1_out;

  Adder #(.width(4)) adder_1 (.a(PC_q), .b(4'b0001), .out(adder_1_out));  // open: cin, cout
  Clock clk (.out(clk_out));
  Register #(.width(4)) PC (.D(adder_1_out), .en(1'b1), .clk(clk_out), .Q(PC_q), .clr(Reset));
  Multiplexer #(.select(4), .width(8)) multiplexer_1 (
    .in0(8'h86), .in1(8'h92), .in2(8'h1), .in3(8'h90), .in4(8'ha0), .in5(8'hb1), .in6(8'h17), .in7(8'h29),
    .in8(8'hf9), .in9(8'hc3), .out(multiplexer_1_out), .sel(PC_q));  // open: in10, in11, in12, in13, in14, in15
  Decoder #(.enable("false"), .select(2)) decoder_1 (
    .out0(decoder_1_out0), .out2(decoder_1_out2), .sel(multiplexer_1_out[7:6]));  // open: out1, out3
  or or_1 (or_1_out, decoder_1_out0, decoder_1_out2);
  or or_2 (or_2_out, decoder_1_out0, decoder_1_out2);
  Shifter shifter_1 (
    .in({{6{1'b0}}, multiplexer_1_out[1:0]}), .\dist ({multiplexer_1_out[3:2], 1'b0}), .out(shifter_1_out));
  Decoder #(.select(2)) decoder_2 (
    .out0(decoder_2_out0), .out1(decoder_2_out1), .out2(decoder_2_out2), .out3(decoder_2_out3),
    .sel(multiplexer_1_out[5:4]), .en(or_2_out));
  and and_1 (and_1_out, or_1_out, decoder_2_out0);
  Multiplexer #(.select(2), .width(8)) multiplexer_2 (
    .in0(adder_2_out), .in2(shifter_1_out), .out(multiplexer_2_out), .sel(multiplexer_1_out[7:6]));  // open: in1, in3
  Register r0 (.D(multiplexer_2_out), .en(and_1_out), .clk(clk_out), .Q(r0_q));  // open: clr
  Multiplexer #(.enable("true"), .select(2), .width(8)) multiplexer_3 (
    .in0(r0_q), .in1(r1_q), .in2(r2_q), .in3(r3_q), .out(multiplexer_3_out), .sel(multiplexer_1_out[3:2]),
    .en(decoder_1_out0));
  and and_2 (and_2_out, or_1_out, decoder_2_out1);
  Register r1 (.D(multiplexer_2_out), .en(and_2_out), .clk(clk_out), .Q(r1_q));  // open: clr
  Multiplexer #(.enable("true"), .select(2), .width(8)) multiplexer_4 (
    .in0(r0_q), .in1(r1_q), .in2(r2_q), .in3(r3_q), .out(multiplexer_4_out), .sel(multiplexer_1_out[1:0]),
    .en(decoder_1_out0));
  Adder adder_2 (.a(multiplexer_4_out), .b(multiplexer_3_out), .out(adder_2_out));  // open: cin, cout
  Register r2 (.D(multiplexer_2_out), .en(and_3_out), .clk(clk_out), .Q(r2_q));  // open: clr
  and and_3 (and_3_out, or_1_out, decoder_2_out2);
  Register r3 (.D(multiplexer_2_out), .en(and_4_out), .clk(clk_out), .Q(r3_q));  // open: clr
  and and_4 (and_4_out, or_1_out, decoder_2_out3);
endmodule

module bner0_sCPU (
  input  Reset
);

  wire and_1_out, and_2_out, and_3_out, and_4_out, and_5_out, clk_out, comparator_1_eq, decoder_1_out0,
       decoder_1_out2, decoder_1_out3, decoder_2_out0, decoder_2_out1, decoder_2_out2, decoder_2_out3,
       not_1_out, or_1_out, or_2_out, or_3_out;
  wire [1:0] multiplexer_4_out;
  wire [3:0] adder_1_out, multiplexer_1_out, PC_q;
  wire [7:0] adder_2_out, multiplexer_2_out, multiplexer_3_out, multiplexer_5_out, multiplexer_6_out, r0_q,
       r1_q, r2_q, r3_q, shifter_1_out;

  Multiplexer #(.width(4)) multiplexer_1 (
    .in0(4'b0001), .in1(multiplexer_2_out[5:2]), .out(multiplexer_1_out), .sel(and_1_out));
  and and_1 (and_1_out, not_1_out, decoder_1_out3);
  Adder #(.width(4)) adder_1 (.a(PC_q), .b(multiplexer_1_out), .out(adder_1_out));  // open: cin, cout
  Register #(.width(4)) PC (.D(adder_1_out), .en(1'b1), .clk(clk_out), .Q(PC_q), .clr(Reset));
  Clock clk (.out(clk_out));
  Multiplexer #(.select(4), .width(8)) multiplexer_2 (
    .in0(8'h86), .in1(8'h92), .in2(8'h1), .in3(8'h90), .in4(8'ha0), .in5(8'hb1), .in6(8'h17), .in7(8'h29),
    .in8(8'hf9), .in9(8'hc3), .out(multiplexer_2_out), .sel(PC_q));  // open: in10, in11, in12, in13, in14, in15
  Decoder #(.enable("false"), .select(2)) decoder_1 (
    .out0(decoder_1_out0), .out2(decoder_1_out2), .out3(decoder_1_out3), .sel(multiplexer_2_out[7:6]));  // open: out1
  or or_1 (or_1_out, decoder_1_out3, decoder_1_out0);
  or or_2 (or_2_out, decoder_1_out0, decoder_1_out2);
  or or_3 (or_3_out, decoder_1_out0, decoder_1_out2);
  Shifter shifter_1 (
    .in({{6{1'b0}}, multiplexer_2_out[1:0]}), .\dist ({multiplexer_2_out[3:2], 1'b0}), .out(shifter_1_out));
  Decoder #(.select(2)) decoder_2 (
    .out0(decoder_2_out0), .out1(decoder_2_out1), .out2(decoder_2_out2), .out3(decoder_2_out3),
    .sel(multiplexer_2_out[5:4]), .en(or_3_out));
  Multiplexer #(.select(2), .width(8)) multiplexer_3 (
    .in0(adder_2_out), .in2(shifter_1_out), .out(multiplexer_3_out), .sel(multiplexer_2_out[7:6]));  // open: in1, in3
  and and_2 (and_2_out, or_2_out, decoder_2_out0);
  Register r0 (.D(multiplexer_3_out), .en(and_2_out), .clk(clk_out), .Q(r0_q));  // open: clr
  Multiplexer #(.select(2), .width(2)) multiplexer_4 (
    .in0(multiplexer_2_out[3:2]), .in3(2'b00), .out(multiplexer_4_out), .sel(multiplexer_2_out[7:6]));  // open: in1, in2
  Multiplexer #(.enable("true"), .select(2), .width(8)) multiplexer_5 (
    .in0(r0_q), .in1(r1_q), .in2(r2_q), .in3(r3_q), .out(multiplexer_5_out), .sel(multiplexer_4_out),
    .en(or_1_out));
  and and_3 (and_3_out, or_2_out, decoder_2_out1);
  Register r1 (.D(multiplexer_3_out), .en(and_3_out), .clk(clk_out), .Q(r1_q));  // open: clr
  Multiplexer #(.enable("true"), .select(2), .width(8)) multiplexer_6 (
    .in0(r0_q), .in1(r1_q), .in2(r2_q), .in3(r3_q), .out(multiplexer_6_out), .sel(multiplexer_2_out[1:0]),
    .en(or_1_out));
  Adder adder_2 (.a(multiplexer_6_out), .b(multiplexer_5_out), .out(adder_2_out));  // open: cin, cout
  Comparator comparator_1 (.a(multiplexer_6_out), .b(multiplexer_5_out), .eq(comparator_1_eq));  // open: gt, lt
  Register r2 (.D(multiplexer_3_out), .en(and_4_out), .clk(clk_out), .Q(r2_q));  // open: clr
  and and_4 (and_4_out, or_2_out, decoder_2_out2);
  not not_1 (not_1_out, comparator_1_eq);
  Register r3 (.D(multiplexer_3_out), .en(and_5_out), .clk(clk_out), .Q(r3_q));  // open: clr
  and and_5 (and_5_out, or_2_out, decoder_2_out3);
endmodule
